# Fritzing sketch Pips_Sketch (saved by Fritzing 0.9.1b)

parts:
  Part1 = LightBlue Bean
  J1 = Piezo Speaker
  S1 = Round Pushbutton
  VCC1 = Battery
  LED1 = Super Flux LED blue [color=Blue]
  R2 = Resistor [tolerance=±5% resistance=10 package="0603 [SMD]"]
  R3 = Resistor [tolerance=±5% resistance=1k package="0603 [SMD]"]
  R4 = Resistor [tolerance=±5% resistance=100 package="0603 [SMD]"]
  R5 = Resistor [tolerance=±5% resistance=10k package="0603 [SMD]"]

nets:
  N1: Part1.VCC, R5.Pin_1
  N2: Part1.D4/MISO, R2.Pin_1
  N3: Part1.D2, R3.Pin_1
  N4: Part1.D0, R4.Pin_1
  N5: Part1.1#102, LED1.cathode, R2.Pin_0
  N6: Part1.1#109, Part1.1#112, Part1.GND, J1.pin1, S1.leg0, VCC1.-, LED1.anode
  N7: Part1.1#111, J1.pin2, R3.Pin_0
  N8: Part1.1#113, S1.leg1, R4.Pin_0, R5.Pin_0
  N9: Part1.BAT, VCC1.+
